# Fritzing sketch Ace Shield 2 (saved by Fritzing 0.9.9b)
circuit board: 6.9709cm x 5.44162cm
breadboards: 1

parts:
  S1 = Toggle Switch [package=THT]
  LINE_4 = LED - 5mm [color="Red (633nm)" current=0.030 package="5 mm [THT]"]
  S2 = Toggle Switch [package=THT]
  LINE_3 = LED - 5mm [color="Red (633nm)" current=0.030 package="5 mm [THT]"]
  R2 = Resistor [tolerance=±5% power=0.25 resistance=220 package=THT]
  OFF = Toggle Switch [package=THT]
  LINE_2 = LED - 5mm [color="Red (633nm)" current=0.030 package="5 mm [THT]"]
  R3 = Resistor [tolerance=±5% power=0.25 resistance=220 package=THT]
  LED_ON_=_Switch_Down = Toggle Switch [package=THT]
  LINE_1 = LED - 5mm [color="Red (633nm)" current=0.030 package="5 mm [THT]"]
  GY_WH_PK_YE_BR_GN = Header 6 [package=molex-1x6-ra]
  R1 = Resistor [tolerance=±5% power=0.25 resistance=220 package=THT]
  Part1 = Arduino Uno (Rev3)

nets:
  N1: S1.L1, LINE_4.anode
  N2: S1.COM, Part1.D5_PWM
  N3: S1.L2, LINE_4.cathode, R1.Pin_1
  N4: S2.L1, LINE_3.anode
  N5: S2.COM, Part1.D6_PWM
  N6: S2.L2, LINE_3.cathode, R2.Pin_1
  N7: R2.Pin_0, GY_WH_PK_YE_BR_GN.2
  N8: OFF.L1, LINE_2.anode
  N9: OFF.COM, Part1.D7
  N10: OFF.L2, LINE_2.cathode, R3.Pin_1
  N11: R3.Pin_0, GY_WH_PK_YE_BR_GN.3
  N12: LED_ON_=_Switch_Down.L1, LINE_1.anode
  N13: LED_ON_=_Switch_Down.COM, Part1.D8
  N14: LED_ON_=_Switch_Down.L2, LINE_1.cathode, GY_WH_PK_YE_BR_GN.4
  N15: GY_WH_PK_YE_BR_GN.1, R1.Pin_0
  N16: GY_WH_PK_YE_BR_GN.5, GY_WH_PK_YE_BR_GN.6, Part1.GND

notes:
  IO Shield
  v22.05-5
  M.Breit
  GRAY
  WHITE
  PINK
  YELLOW
  BROWN
  GREEN
  Ace-C-U-L
  Switches:
  LED ON  = UP
  LED OFF = DOWN
